# Fritzing sketch alim (saved by Fritzing 0.9.0b)
circuit board: 2.99961cm x 4.99091cm
perfboards: 1

parts:
  R1 = Resistor [tolerance=±5% resistance=220 package=THT]
  C1 = Electrolytic Capacitor [capacitance=1µF package="100 mil [THT, electrolytic]"]
  C2 = Electrolytic Capacitor [capacitance=1µF package="100 mil [THT, electrolytic]"]
  C3 = Electrolytic Capacitor [capacitance=1µF package="100 mil [THT, electrolytic]"]
  U1 = Voltage Regulator [package=to220-adj]
  U2 = Voltage Regulator [package=to220-adj]
  J2 = female pin header, 2 pins [form="♀ (female)"]
  J3 = female pin header, 2 pins [form="♀ (female)"]
  J1 = female pin header, 2 pins [form="♀ (female)"]
  J4 = female pin header, 1 pin [form="♀ (female)"]
  LED1 = LED - 5mm [color="Red (633nm)" package="5 mm [THT]"]

nets:
  N1: R1.Pin_0, C2.+, U2.OUT, J2.pin2
  N2: R1.Pin_1, LED1.cathode
  N3: C1.-, C2.-, C3.-, U1.OUT, U2.ADJ, J2.pin1, J3.pin2, J1.pin1, J4.pin1, LED1.anode
  N4: C1.+, U1.IN, J1.pin2
  N5: C3.+, U1.ADJ, U2.IN, J3.pin1
