# Fritzing sketch atmega (saved by Fritzing 0.9.0b)
circuit board: 5.39075cm x 2.38874cm
breadboards: 1

parts:
  IC1 = MICROCONTROLLER [package=dil28-3]
  LED1 = LED - 3mm [color="Red (633nm)" package="3 mm [THT]"]
  R1 = Resistor [tolerance=±5% resistance=10k package=THT]
  R2 = Resistor [tolerance=±5% resistance=330 package=THT]
  XTAL1 = Crystal [frequency="16 Mhz" package=THT]
  C1 = Capacitor [package=cap-pth-small2]
  C2 = Capacitor [package=cap-pth-small2]
  J4 = female pin header, 4 pins [form="♀ (female)"]
  J5 = female pin header, 4 pins [form="♀ (female)"]
  J6 = female pin header, 6 pins [form="♀ (female)"]
  J7 = female pin header, 1 pin [form="♀ (female)"]
  J3 = female pin header, 7 pins [form="♀ (female)"]

nets:
  N1: IC1.PC6(_RESET), J6.pin1
  N2: IC1.PD0(RXD), J6.pin2
  N3: IC1.PD1(TXD), J6.pin3
  N4: IC1.PD2(INT0), J6.pin4
  N5: IC1.PD3(INT1), J6.pin5
  N6: IC1.PD4(XCK_T0), J6.pin6
  N7: IC1.VCC, IC1.AREF, R2.Pin_0, C1.2, C2.2, J3.pin7
  N8: IC1.GND, J7.pin1
  N9: IC1.PB6(XTAL1_TOSC1), IC1.AGND, R1.Pin_1, J3.pin1
  N10: IC1.PB7(XTAL2_TOSC2), LED1.cathode
  N11: IC1.PD5(T1), J5.pin1
  N12: IC1.PD6(AIN0), J5.pin2
  N13: IC1.PD7(AIN1), J5.pin3
  N14: IC1.PB0(ICP), J5.pin4
  N15: IC1.PB1(OC1A), J4.pin4
  N16: IC1.PB2(SS_OC1B), J4.pin3
  N17: IC1.PB3(MOSI_OC2), J4.pin2
  N18: IC1.PB4(MISO), J4.pin1
  N19: IC1.PB5(SCK), XTAL1.pin_0, C1.1
  N20: IC1.AVCC, XTAL1.pin_1, C2.1
  N21: IC1.PC0(ADC0), J3.pin6
  N22: IC1.PC1(ADC1), J3.pin5
  N23: IC1.PC2(ADC2), J3.pin4
  N24: IC1.PC3(ADC3), J3.pin3
  N25: IC1.PC4(ADC4_SDA), J3.pin2
  N26: IC1.PC5(ADC5_SCL), R1.Pin_0
  N27: LED1.anode, R2.Pin_1
